// Logisim project DCNN.circ as structural Verilog: 10 circuits, main circuit main
module main (
  input  Rst,
  input  Start,
  input  Clk,
  input  Stride,
  input  Filter_Size,
  input  Instr,
  output Done
);

  wire alu_1_byte, controller_1_en_alu, controller_1_en_dma, dma_1_en_cache, dma_1_en_ram, dma_1_r_w_cache,
       dma_1_r_w_ram, dma_1_read_filter, or_1_out;
  wire [1:0] controller_1_ctrl;
  wire [2:0] dma_1_cahce_row;
  wire [4:0] ram_1_data_out;
  wire [7:0] dma_1_cache_col;
  wire [17:0] dma_1_ram_addr;
  wire [24:0] filter_cache_1_filter_out, img_cache_1_img_out;

  or or_1 (or_1_out, Rst, Done);
  DMA dma_1 (
    .Reset(or_1_out), .En(controller_1_en_dma), .Clk(Clk), .Stride(Stride), .Filt_Sz(Filter_Size),
    .Ctrl(controller_1_ctrl), .En_Ram(dma_1_en_ram), .R_W_Ram(dma_1_r_w_ram), .Ram_Addr(dma_1_ram_addr),
    .En_Cache(dma_1_en_cache), .R_W_Cache(dma_1_r_w_cache), .Cahce_Row(dma_1_cahce_row),
    .Cache_Col(dma_1_cache_col), .Read_Filter(dma_1_read_filter), .Done(Done));
  Controller controller_1 (
    .Rst(or_1_out), .Clk(Clk), .Start(Start), .Filter_Size(Filter_Size), .Ctrl(controller_1_ctrl),
    .En_DMA(controller_1_en_dma), .En_ALU(controller_1_en_alu));
  Filter_Cache filter_cache_1 (
    .Rst(or_1_out), .Clk(Clk), .En(dma_1_read_filter), .Size(Filter_Size), .Filter_In(ram_1_data_out),
    .Filter_Out(filter_cache_1_filter_out));
  Ram ram_1 (
    .Rst(or_1_out), .Clk(Clk), .En(dma_1_en_ram), .R_W(dma_1_r_w_ram), .Addr(dma_1_ram_addr),
    .Data_In(alu_1_byte), .Data_Out(ram_1_data_out));
  Img_Cache img_cache_1 (
    .Rst(or_1_out), .Clk(Clk), .En(dma_1_en_cache), .R_W(dma_1_r_w_cache), .Row(dma_1_cahce_row),
    .Col(dma_1_cache_col), .Img_In(ram_1_data_out), .Img_Out(img_cache_1_img_out));
  ALU alu_1 (
    .Rst(or_1_out), .Clk(Clk), .En(controller_1_en_alu), .Window(img_cache_1_img_out),
    .Filter(filter_cache_1_filter_out), .Instr(Instr), .Byte(alu_1_byte));
endmodule

module DMA (
  input  Reset,
  input  En,
  input  Clk,
  input  Stride,
  input  Filt_Sz,
  input  [1:0] Ctrl,
  output En_Ram,
  output R_W_Ram,
  output [17:0] Ram_Addr,
  output En_Cache,
  output R_W_Cache,
  output [2:0] Cahce_Row,
  output [7:0] Cache_Col,
  output Read_Filter,
  output Done
);

  wire and_1_out, not_1_out, not_2_out;
  wire [2:0] multiplexer_1_out;
  wire [17:0] Filter_Address_q, Read_Address_q, Write_Address_q;

  Multiplexer #(.width(3), .enable("false")) multiplexer_1 (
    .in0(3'b011), .in1(3'b101), .out(multiplexer_1_out), .sel(Filt_Sz));
  Counter #(.width(18), .max('h3ffff)) Filter_Address (
    .clr(Reset), .count(Ctrl[1]), .clk(Clk), .D({18{1'b1}}), .Q(Filter_Address_q));  // open: load, up, carry
  not not_1 (not_1_out, Ctrl[1]);
  and and_1 (and_1_out, Ctrl[0], not_1_out);
  Counter #(.width(18), .max('h3ffff)) Read_Address (
    .clr(Reset), .count(and_1_out), .clk(Clk), .D({18{1'b1}}), .Q(Read_Address_q));  // open: load, up, carry
  Counter #(.width(18), .max('h3ffff)) Write_Address (
    .clr(Reset), .count(not_2_out), .clk(Clk), .D({18{1'b1}}), .Q(Write_Address_q));  // open: load, up, carry
  not not_2 (not_2_out, and_1_out);
  Multiplexer #(.select(2), .width(18), .enable("false")) multiplexer_2 (
    .in0(Write_Address_q), .in1(Read_Address_q), .in2(Filter_Address_q), .in3(Filter_Address_q),
    .out(Ram_Addr), .sel(Ctrl));

  assign En_Ram = En;
endmodule

module Img_Cache (
  input  Rst,
  input  Clk,
  input  En,
  input  R_W,
  input  [2:0] Row,
  input  [7:0] Col,
  input  [4:0] Img_In,
  output [24:0] Img_Out
);
endmodule

module Controller (
  input  Rst,
  input  Clk,
  input  Start,
  input  Filter_Size,
  output [1:0] Ctrl,
  output En_DMA,
  output En_ALU
);

  wire comparator_1_eq, comparator_1_gt, comparator_2_eq, comparator_2_gt, or_1_out, or_2_out, or_3_out,
       Row_Counter_carry;
  wire [2:0] Filter_Counter_q, multiplexer_1_out;
  wire [7:0] Row_Counter_q;

  D_Flip_Flop d_ff_1 (.D(or_1_out), .clk(Clk), .Q(En_DMA), .reset(Rst));  // open: Qn, preset
  or or_1 (or_1_out, En_DMA, Start);
  Counter #(.width(3), .max('h5), .ongoal("stay")) Filter_Counter (
    .clr(Rst), .count(En_DMA), .clk(Clk), .Q(Filter_Counter_q));  // open: load, up, D, carry
  Multiplexer #(.width(3), .enable("false")) multiplexer_1 (
    .in0(3'b011), .in1(3'b101), .out(multiplexer_1_out), .sel(Filter_Size));
  Comparator #(.width(3)) comparator_1 (
    .a(multiplexer_1_out), .b(Filter_Counter_q), .gt(comparator_1_gt), .eq(comparator_1_eq));  // open: lt
  or or_2 (or_2_out, comparator_1_gt, comparator_1_eq);
  Counter #(.ongoal("stay")) Row_Counter (
    .clr(Rst), .count(or_2_out), .clk(Clk), .carry(Row_Counter_carry), .Q(Row_Counter_q));  // open: load, up, D
  Counter #(.width(3), .max('h5)) State_Counter (
    .clr(Rst), .count(Row_Counter_carry), .clk(Clk), .carry(Ctrl[1]));  // open: load, up, D, Q
  not not_1 (Ctrl[0], or_2_out);
  Comparator comparator_2 (.a(Row_Counter_q), .b({8{1'b1}}), .gt(comparator_2_gt), .eq(comparator_2_eq));  // open: lt
  or or_3 (or_3_out, comparator_2_gt, comparator_2_eq);
  and and_1 (En_ALU, Ctrl[1], or_3_out);

  // Notes on the sheet:
  //   1x Filter
  //   00 Write
  //   01 Read
endmodule

module ALU (
  input  Rst,
  input  Clk,
  input  En,
  input  [24:0] Window,
  input  [24:0] Filter,
  input  Instr,
  output Byte
);

  wire [16:0] alu_buffer_1_a_out, alu_buffer_1_p_out, alu_buffer_1_s_out, undriven, undriven_2, undriven_3;

  ALU_Buffer alu_buffer_1 (
    .A_In(undriven_3), .S_In(undriven_2), .P_In(undriven), .Rst(Rst), .Clk(Clk), .En(En),
    .A_Out(alu_buffer_1_a_out), .S_Out(alu_buffer_1_s_out), .P_Out(alu_buffer_1_p_out));
  ALU_Stage_Unit alu_stage_unit_1 (
    .A_In(alu_buffer_1_a_out), .S_In(alu_buffer_1_s_out), .P_In(alu_buffer_1_p_out));  // open: A_Out, S_Out, P_Out
endmodule

module Ram (
  input  Rst,
  input  Clk,
  input  En,
  input  R_W,
  input  [17:0] Addr,
  input  Data_In,
  output [4:0] Data_Out
);
endmodule

// +
module ALU_Buffer (
  input  [16:0] A_In,
  input  [16:0] S_In,
  input  [16:0] P_In,
  input  Rst,
  input  Clk,
  input  En,
  output [16:0] A_Out,
  output [16:0] S_Out,
  output [16:0] P_Out
);

  Register #(.width(17)) A_Reg (.D(A_In), .en(En), .clk(Clk), .Q(A_Out), .clr(Rst));
  Register #(.width(17)) S_Reg (.D(S_In), .en(En), .clk(Clk), .Q(S_Out), .clr(Rst));
  Register #(.width(17)) P_Reg (.D(P_In), .en(En), .clk(Clk), .Q(P_Out), .clr(Rst));
endmodule

module ALU_Stage_Unit (
  input  [16:0] A_In,
  input  [16:0] S_In,
  input  [16:0] P_In,
  output [16:0] A_Out,
  output [16:0] S_Out,
  output [16:0] P_Out
);

  wire [0:0] adder_1_out;
  wire [16:0] multiplexer_1_out;

  Multiplexer #(.select(2), .width(17), .enable("false")) multiplexer_1 (
    .in0({17{1'b0}}), .in1(A_In), .in2(S_In), .in3({17{1'b0}}), .out(multiplexer_1_out));  // open: sel
  Adder #(.width(17)) adder_1 (
    .a(multiplexer_1_out), .b(P_In), .out({P_Out[1], P_Out[16:2], adder_1_out[0]}));  // open: cin, cout

  assign A_Out = A_In;
  assign P_Out[0] = P_Out[1];
  assign S_Out = S_In;
endmodule

module Filter_Cache (
  input  Rst,
  input  Clk,
  input  En,
  input  Size,
  input  [4:0] Filter_In,
  output [24:0] Filter_Out
);

  wire decoder_1_out0;
  wire [2:0] counter_1_q;

  Counter #(.width(3), .max('h7)) counter_1 (
    .clr(Rst), .load(1'b0), .up(1'b1), .count(En), .clk(Clk), .Q(counter_1_q));  // open: D, carry
  Decoder #(.select(3)) decoder_1 (
    .out0(decoder_1_out0), .sel(counter_1_q), .en(En));  // open: out1, out2, out3, out4, out5, out6, out7
  Register #(.width(1)) register_1 ();  // open: D, en, Q, clk, clr
endmodule

module ALU_Stage (
  input  [16:0] A0_In,
  input  [16:0] A1_in,
  input  [16:0] in_3,
  input  [16:0] S0_In,
  input  [16:0] in_5,
  input  [16:0] in_6,
  input  [16:0] P0_In,
  input  [16:0] in_8,
  input  [16:0] in_9,
  input  [16:0] A3_In,
  input  [16:0] in_11,
  input  [16:0] in_12,
  input  [16:0] in_13,
  input  [16:0] in_14,
  input  [16:0] in_15,
  input  [16:0] in_16,
  input  [16:0] in_17,
  input  [16:0] in_18,
  input  [16:0] in_19,
  input  [16:0] in_20,
  input  [16:0] in_21,
  input  [16:0] in_22,
  input  [16:0] in_23,
  input  [16:0] in_24,
  input  [16:0] in_25,
  input  [16:0] in_26,
  input  [16:0] in_27,
  input  [16:0] in_28,
  input  [16:0] in_29,
  input  [16:0] in_30,
  input  [16:0] in_31,
  input  [16:0] in_32,
  input  [16:0] in_33,
  input  [16:0] in_34,
  input  [16:0] in_35,
  input  [16:0] in_36,
  input  [16:0] in_37,
  input  [16:0] in_38,
  input  [16:0] in_39,
  input  [16:0] in_40,
  input  [16:0] in_41,
  input  [16:0] in_42,
  input  [16:0] in_43,
  input  [16:0] in_44,
  input  [16:0] in_45,
  output [16:0] A0_Out,
  output [16:0] out_47,
  output [16:0] out_48,
  output [16:0] S0_Out,
  output [16:0] out_50,
  output [16:0] out_51,
  output [16:0] P0_Out,
  output [16:0] out_53,
  output [16:0] out_54,
  output [16:0] out_55,
  output [16:0] out_56,
  output [16:0] out_57,
  output [16:0] out_58,
  output [16:0] out_59,
  output [16:0] out_60,
  output [16:0] out_61,
  output [16:0] out_62,
  output [16:0] out_63,
  output [16:0] out_64,
  output [16:0] out_65,
  output [16:0] out_66,
  output [16:0] out_67,
  output [16:0] out_68,
  output [16:0] out_69,
  output [16:0] out_70,
  output [16:0] out_71,
  output [16:0] out_72,
  output [16:0] out_73,
  output [16:0] out_74,
  output [16:0] out_75,
  output [16:0] out_76,
  output [16:0] out_77,
  output [16:0] out_78,
  output [16:0] out_79,
  output [16:0] out_80,
  output [16:0] out_81,
  output [16:0] out_82,
  output [16:0] out_83,
  output [16:0] out_84,
  output [16:0] out_85,
  output [16:0] out_86,
  output [16:0] out_87,
  output [16:0] out_88,
  output [16:0] out_89,
  output [16:0] out_90
);

  ALU_Stage_Unit alu_stage_unit_1 (
    .A_In(A0_In), .S_In(S0_In), .P_In(P0_In), .A_Out(A0_Out), .S_Out(S0_Out), .P_Out(P0_Out));
  ALU_Stage_Unit alu_stage_unit_2 (
    .A_In(A3_In), .S_In(in_13), .P_In(in_16), .A_Out(out_55), .S_Out(out_58), .P_Out(out_61));
  ALU_Stage_Unit alu_stage_unit_3 (
    .A_In(in_19), .S_In(in_22), .P_In(in_25), .A_Out(out_64), .S_Out(out_67), .P_Out(out_70));
  ALU_Stage_Unit alu_stage_unit_4 (
    .A_In(in_28), .S_In(in_31), .P_In(in_34), .A_Out(out_73), .S_Out(out_76), .P_Out(out_79));
  ALU_Stage_Unit alu_stage_unit_5 (
    .A_In(in_37), .S_In(in_40), .P_In(in_43), .A_Out(out_82), .S_Out(out_85), .P_Out(out_88));
  ALU_Stage_Unit alu_stage_unit_6 (
    .A_In(A1_in), .S_In(in_5), .P_In(in_8), .A_Out(out_47), .S_Out(out_50), .P_Out(out_53));
  ALU_Stage_Unit alu_stage_unit_7 (
    .A_In(in_11), .S_In(in_14), .P_In(in_17), .A_Out(out_56), .S_Out(out_59), .P_Out(out_62));
  ALU_Stage_Unit alu_stage_unit_8 (
    .A_In(in_20), .S_In(in_23), .P_In(in_26), .A_Out(out_65), .S_Out(out_68), .P_Out(out_71));
  ALU_Stage_Unit alu_stage_unit_9 (
    .A_In(in_29), .S_In(in_32), .P_In(in_35), .A_Out(out_74), .S_Out(out_77), .P_Out(out_80));
  ALU_Stage_Unit alu_stage_unit_10 (
    .A_In(in_38), .S_In(in_41), .P_In(in_44), .A_Out(out_83), .S_Out(out_86), .P_Out(out_89));
  ALU_Stage_Unit alu_stage_unit_11 (
    .A_In(in_3), .S_In(in_6), .P_In(in_9), .A_Out(out_48), .S_Out(out_51), .P_Out(out_54));
  ALU_Stage_Unit alu_stage_unit_12 (
    .A_In(in_12), .S_In(in_15), .P_In(in_18), .A_Out(out_57), .S_Out(out_60), .P_Out(out_63));
  ALU_Stage_Unit alu_stage_unit_13 (
    .A_In(in_21), .S_In(in_24), .P_In(in_27), .A_Out(out_66), .S_Out(out_69), .P_Out(out_72));
  ALU_Stage_Unit alu_stage_unit_14 (
    .A_In(in_30), .S_In(in_33), .P_In(in_36), .A_Out(out_75), .S_Out(out_78), .P_Out(out_81));
  ALU_Stage_Unit alu_stage_unit_15 (
    .A_In(in_39), .S_In(in_42), .P_In(in_45), .A_Out(out_84), .S_Out(out_87), .P_Out(out_90));
endmodule
